# Fritzing sketch garage_door_opener (saved by Fritzing 1.0.1rc)
breadboards: 1

parts:
  S1 = Momentary Switch [package=ksa_sealed_tac_switch]
  S2 = Momentary Switch [package=ksa_sealed_tac_switch]
  S3 = Momentary Switch [package=ksa_sealed_tac_switch]
  S4 = Momentary Switch [package=ksa_sealed_tac_switch]
  S5 = Momentary Switch [package=ksa_sealed_tac_switch]
  Mod1 = Raspberry Pi Pico
  LED1 = LED - 5mm [color="Red (633nm)" current=0.030A package="5 mm [THT]"]
  LED2 = LED - 5mm [color="Red (633nm)" current=0.030A package="5 mm [THT]"]
  R1 = Resistor [tolerance=±5% power=0.25W resistance=330 package=THT]
  R2 = Resistor [tolerance=±5% power=0.25W resistance=330 package=THT]
  R3 = Resistor [tolerance=±5% power=0.25W resistance=330 package=THT]
  R4 = Resistor [tolerance=±5% power=0.25W resistance=330 package=THT]
  R5 = Resistor [tolerance=±5% power=0.25W resistance=330 package=THT]
  R6 = Resistor [tolerance=±5% power=0.25W resistance=330 package=THT]
  LED3 = LED - 5mm [color="Green (560nm)" current=0.030A package="5 mm [THT]"]
  LED4 = LED - 5mm [color="Green (565nm)" current=0.030A package="5 mm [THT]"]
  LED5 = LED - 5mm [color="Yellow (595nm)" current=0.030A package="5 mm [THT]"]
  LED6 = LED - 5mm [color="Yellow (595nm)" current=0.030A package="5 mm [THT]"]
  R7 = Resistor [tolerance=±5% power=0.25W resistance=4.7k package=THT]
  R8 = Resistor [tolerance=±5% power=0.25W resistance=4.7k package=THT]
  R9 = Resistor [tolerance=±5% power=0.25W resistance=4.7k package=THT]
  R10 = Resistor [tolerance=±5% power=0.25W resistance=4.7k package=THT]
  R11 = Resistor [tolerance=±5% power=0.25W resistance=4.7k package=THT]
  S6 = Toggle Switch [package=THT]
  R12 = Resistor [tolerance=±5% power=0.25W resistance=4.7k package=THT]
  LED7 = LED - 5mm [color="Green (565nm)" current=0.030A package="5 mm [THT]"]
  R13 = Resistor [tolerance=±5% power=0.25W resistance=330 package=THT]

nets:
  N1: S1.1, Mod1.pin_26, R11.Pin_0
  N2: S1.3, S2.1, S3.1, S4.1, S5.3, Mod1.pin_36, S6.L2
  N3: S2.3, Mod1.pin_25, R10.Pin_0
  N4: S3.3, Mod1.pin_24, R9.Pin_0
  N5: S4.3, Mod1.pin_22, R8.Pin_0
  N6: S5.1, Mod1.pin_21, R7.Pin_0
  N7: Mod1.pin_3, Mod1.pin_8, Mod1.pin_13, Mod1.pin_18, Mod1.pin_23, Mod1.pin_28, Mod1.pin_33, Mod1.pin_38, Mod1.pin_42, LED1.cathode, LED2.cathode, R3.Pin_0, R4.Pin_0, R5.Pin_0, R6.Pin_0, R7.Pin_1, R8.Pin_1, R9.Pin_1, R10.Pin_1, R11.Pin_1, S6.L1, R12.Pin_1, LED7.cathode
  N8: Mod1.pin_12, R13.Pin_1
  N9: Mod1.pin_14, LED3.anode
  N10: Mod1.pin_15, LED4.anode
  N11: Mod1.pin_16, LED6.anode
  N12: Mod1.pin_17, LED5.anode
  N13: Mod1.pin_19, R2.Pin_1
  N14: Mod1.pin_20, R1.Pin_1
  N15: Mod1.pin_27, S6.COM, R12.Pin_0
  N16: LED1.anode, R1.Pin_0
  N17: LED2.anode, R2.Pin_0
  N18: R3.Pin_1, LED5.cathode
  N19: R4.Pin_1, LED6.cathode
  N20: R5.Pin_1, LED4.cathode
  N21: R6.Pin_1, LED3.cathode
  N22: LED7.anode, R13.Pin_0

notes:
  The 4.7k pulldown resistors for the switches (7 - R12) are neccessary if you use a pico2 A2 stepping because of its bug "E9"

custom parts:
  Raspberry Pi Pico: Raspberry Pi Pico. Based around the RP2040 microcontroller the Pico is a low cost microcontroller device bringing Raspberry Pi quality, cost, and easy of use to the microcontroller space. Jan 2021, Split part in to two versions: tht (this one) and SMD. This one will drill holes for a .1 in header in pcb to allow plugging in the module as well as providing pads to solder the module to the top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
